// Logisim project Contadorfechado.circ as structural Verilog: 2 circuits, main circuit main
module main (
  input  in_1,
  input  in_2,
  output [7:0] out_3
);

  wire and_1_out, and_2_out, and_3_out, and_4_out, and_5_out, and_6_out;

  T_Flip_Flop #(.NegatePresetClear("true")) t_ff_1 (
    .clk(in_1), .T(1'b1), .Q(out_3[0]), .reset(in_2));  // open: Qn, preset
  T_Flip_Flop #(.NegatePresetClear("true")) t_ff_2 (
    .clk(in_1), .T(out_3[0]), .Q(out_3[1]), .reset(in_2));  // open: Qn, preset
  and and_1 (and_1_out, out_3[1], out_3[0]);
  T_Flip_Flop #(.NegatePresetClear("true")) t_ff_3 (
    .clk(in_1), .T(and_1_out), .Q(out_3[2]), .reset(in_2));  // open: Qn, preset
  and and_2 (and_2_out, out_3[2], and_1_out);
  T_Flip_Flop #(.NegatePresetClear("true")) t_ff_4 (
    .clk(in_1), .T(and_2_out), .Q(out_3[3]), .reset(in_2));  // open: Qn, preset
  and and_3 (and_3_out, out_3[3], and_2_out);
  T_Flip_Flop #(.NegatePresetClear("true")) t_ff_5 (
    .clk(in_1), .T(and_3_out), .Q(out_3[4]), .reset(in_2));  // open: Qn, preset
  and and_4 (and_4_out, out_3[4], and_3_out);
  T_Flip_Flop #(.NegatePresetClear("true")) t_ff_6 (
    .clk(in_1), .T(and_4_out), .Q(out_3[5]), .reset(in_2));  // open: Qn, preset
  and and_5 (and_5_out, out_3[5], and_4_out);
  T_Flip_Flop #(.NegatePresetClear("true")) t_ff_7 (
    .clk(in_1), .T(and_5_out), .Q(out_3[6]), .reset(in_2));  // open: Qn, preset
  and and_6 (and_6_out, out_3[6], and_5_out);
  T_Flip_Flop #(.NegatePresetClear("true")) t_ff_8 (
    .clk(in_1), .T(and_6_out), .Q(out_3[7]), .reset(in_2));  // open: Qn, preset

  // Notes on the sheet:
  //   Q1
endmodule

module l (
);

  main main_1 ();  // open: in_1, out_3, in_2
endmodule
